# Fritzing sketch ESP32MQTT433BridgeDog (saved by Fritzing 0.9.3b)
stripboards: 1

parts:
  R2 = Resistor [tolerance=±5% resistance=330 package=THT]  # not connected
  DHT22 = Humidity and Temperature Sensor RHT03
  R3 = Resistor [tolerance=±5% resistance=10k package=THT]  # not connected
  ESPDEVKITV1_LHS = ESP32 DEVKITV1 LHS - 15 pins [form="♀ (female)" package=THT]
  ESPDEVKITV1_RHS = ESP32 DEVKITV1 RHS - 15 pins [form="♀ (female)" package=THT]
  LED1 = smd LED [color="Green (570nm)" package="0603 [SMD]"]  # not connected
  LED2 = smd LED [color="Red (635nm)" package="0603 [SMD]"]  # not connected
  DHT22_2 = male pin header, 3 pins [form="♂ (male)"]
  J2 = female pin header, 3 pins [form="♀ (female)"]  # not connected
  J1 = female pin header, 3 pins [form="♀ (female)"]
  OLED_I2C = OLED I2C header [form="♂ (male)" package=THT]  # not connected
  Part1 = NRF24L01+ Breakout Board  # not connected
  nrfL24L01+1 = nrf24l01+ [form="♂ (male)" package=THT]  # not connected
  433Tx1 = 433Mhz Transmitter - 3 pins [form="♂ (male)" package=THT]

nets:
  N1: DHT22.Vcc, J1.pin3
  N2: DHT22.Data-signal, J1.pin2
  N3: DHT22.GND_1, J1.pin1
  GND: ESPDEVKITV1_LHS.GND, ESPDEVKITV1_RHS.GND, DHT22_2.pin1, 433Tx1.GND
  N4: ESPDEVKITV1_LHS.GPIO32, 433Tx1.data
  3.3V: ESPDEVKITV1_RHS.VDD_3V3, DHT22_2.pin3, 433Tx1.Vcc

notes:
  DEVKIT V1
  row spacing 10 holes
  row1 to 11
  GPIO 36
  (ADC 0)
  GPIO 23
  (DHT22)
  SDA GPIO 21
  SCL GPIO 22

custom parts:
  OLED I2C header: Generic male header
  nrf24l01+: Generic male header
  433Mhz Transmitter - 3 pins: 433Mhz Transmitter
